// Logisim project Kasm.circ as structural Verilog: 8 circuits, main circuit main
module main (
  input  Manual,
  input  [15:0] ManualINST
);

  wire clk, clock_1_out, d_ff_1_qn, demultiplexer_1_out0, demultiplexer_2_out0, FetchReg, HALT, IO, JMPIF,
       JUMP, LOAD, LOADI, MATH, multiplexer_5_out, NOOP, not_1_out, or_1_out, or_2_out, or_3_out, or_4_out,
       or_5_out, RESET_out, RIO, status, STORE, WIO, WIOIH, WIOIL;
  wire [1:0] Func2, Func3;
  wire [2:0] controlled_buffer_3_out, Rb;
  wire [5:0] Arithmetic_Logic_Unit_status, ImmV, register_1_q;
  wire [6:0] keyboard_1_data;
  wire [15:0] Addr, Arithmetic_Logic_Unit_numout, controlled_buffer_1_out, Data, FetchedInst,
       Instruction_Register_q, multiplexer_1_out, multiplexer_2_out, multiplexer_4_out, Program_Counter_q,
       Register_Bank_out_a, Register_Bank_out_b, Register_Bank_out_d, RIODATA, rom_1_data;
  wire [15:13] multiplexer_3_out;

  RAM #(.addrWidth(16), .dataWidth(16), .databus("bidir"), .readbehav("war")) ram_1 (
    .addr(Addr), .we(STORE), .oe(LOAD), .clk(clk));  // open: data
  not not_1 (not_1_out, FetchReg);
  Counter #(.max('hffff), .width(16)) Program_Counter (
    .load(JUMP), .D(Addr), .count(not_1_out), .Q(Program_Counter_q), .clk(clk), .clr(RESET_out));  // open: carry, up
  ROM #(.addrWidth(16), .dataWidth(16)) rom_1 (.addr(Program_Counter_q), .data(rom_1_data));
  TTY tty_1 (.data(Data[6:0]), .clk(clk), .we(demultiplexer_1_out0), .clr(RESET_out));
  Keyboard keyboard_1 (.clk(clk), .re(demultiplexer_2_out0), .data(keyboard_1_data));  // open: clr, avail
  assign controlled_buffer_1_out = LOAD ? Data : 16'bz;  // Controlled_Buffer controlled_buffer_1
  assign controlled_buffer_1_out = LOADI ? multiplexer_1_out : 16'bz;  // Controlled_Buffer controlled_buffer_2
  Multiplexer #(.width(16)) multiplexer_1 (
    .in0({{8{1'b0}}, Func3, ImmV}), .in1({Func3, ImmV, {8{1'b0}}}), .out(multiplexer_1_out), .sel(Func2[0]));
  or or_1 (or_1_out, MATH, LOAD, LOADI, RIO);
  assign controlled_buffer_3_out = or_2_out ? Rb : 3'bz;  // Controlled_Buffer controlled_buffer_3
  or or_2 (or_2_out, LOAD, LOADI);
  assign controlled_buffer_3_out = or_3_out ? ImmV[5:3] : 3'bz;  // Controlled_Buffer controlled_buffer_4
  assign controlled_buffer_1_out = RIO ? RIODATA : 16'bz;  // Controlled_Buffer controlled_buffer_5
  assign controlled_buffer_1_out = MATH ? Arithmetic_Logic_Unit_numout : 16'bz;  // Controlled_Buffer controlled_buffer_6
  or or_3 (or_3_out, MATH, JMPIF, RIO);
  assign RIODATA = {{9{1'b0}}, keyboard_1_data};  // Bit_Extender bit_extender_1
  Multiplexer #(.width(16)) multiplexer_2 (
    .in0(rom_1_data), .in1(FetchedInst), .out(multiplexer_2_out), .sel(FetchReg));
  Clock clock_1 (.out(clock_1_out));
  D_Flip_Flop d_ff_1 (.D(HALT), .clk(HALT), .Qn(d_ff_1_qn), .reset(RESET_out));  // open: Q, preset
  Button RESET (.out(RESET_out));
  Register #(.width(16)) Instruction_Register (
    .D(multiplexer_2_out), .en(1'b1), .clk(clk), .Q(Instruction_Register_q), .clr(RESET_out));
  assign clk = d_ff_1_qn ? clock_1_out : 1'bz;  // Controlled_Buffer controlled_buffer_7
  or or_4 (or_4_out, WIOIL, WIO, WIOIH);
  Demultiplexer #(.select(3)) demultiplexer_1 (
    .out0(demultiplexer_1_out0), .in(or_4_out), .sel(Rb));  // open: out1, out2, out3, out4, out5, out6, out7
  Demultiplexer #(.select(3)) demultiplexer_2 (
    .out0(demultiplexer_2_out0), .in(RIO), .sel(Rb));  // open: out1, out2, out3, out4, out5, out6, out7
  assign Addr = STORE ? Register_Bank_out_a : 16'bz;  // Controlled_Buffer controlled_buffer_8
  RegisterBank Register_Bank (
    .clk(clk), .in_val(controlled_buffer_1_out), .Write(or_1_out), .Ra(ImmV[2:0]),
    .Rd(controlled_buffer_3_out), .Rb(Rb), .out_a(Register_Bank_out_a), .out_b(Register_Bank_out_b),
    .out_d(Register_Bank_out_d));
  assign Addr = LOAD ? Register_Bank_out_a : 16'bz;  // Controlled_Buffer controlled_buffer_9
  assign Addr = JMPIF ? Register_Bank_out_d : 16'bz;  // Controlled_Buffer controlled_buffer_10
  assign Data = STORE ? Register_Bank_out_b : 16'bz;  // Controlled_Buffer controlled_buffer_11
  assign FetchedInst = FetchReg ? Register_Bank_out_b : 16'bz;  // Controlled_Buffer controlled_buffer_12
  Multiplexer #(.width(16)) multiplexer_3 (
    .in0(Instruction_Register_q), .in1(ManualINST), .out({multiplexer_3_out, Func2, Func3, ImmV, Rb}),
    .sel(Manual));
  // Probe on ManualINST
  assign Data = WIO ? Register_Bank_out_a : 16'bz;  // Controlled_Buffer controlled_buffer_13
  Decoder #(.enable("false"), .select(3)) decoder_1 (
    .out0(NOOP), .out1(MATH), .out2(LOAD), .out3(LOADI), .out4(STORE), .out5(JMPIF), .out6(IO), .out7(HALT),
    .sel(multiplexer_3_out));
  Demultiplexer #(.select(2)) demultiplexer_3 (
    .out0(RIO), .out1(WIO), .out2(WIOIL), .out3(WIOIH), .in(IO), .sel(Func2));
  and and_1 (status, MATH, Func2[1]);
  Register #(.width(6)) register_1 (
    .D(Arithmetic_Logic_Unit_status), .en(1'b1), .clk(clk), .Q(register_1_q));  // open: clr
  ArithmeticLogicUnit Arithmetic_Logic_Unit (
    .NumA(Register_Bank_out_a), .NumB(Register_Bank_out_b), .Sel({Func2, Func3}),
    .NumOut(Arithmetic_Logic_Unit_numout), .Status(Arithmetic_Logic_Unit_status));
  or or_5 (or_5_out, WIOIH, WIOIL);
  assign Data = or_5_out ? multiplexer_4_out : 16'bz;  // Controlled_Buffer controlled_buffer_14
  Multiplexer #(.width(16)) multiplexer_4 (
    .in0({{8{1'b0}}, Func3, ImmV}), .in1({Func3, ImmV, {8{1'b0}}}), .out(multiplexer_4_out), .sel(WIOIH));
  Multiplexer #(.select(3)) multiplexer_5 (
    .in0(register_1_q[0]), .in1(register_1_q[1]), .in2(register_1_q[2]), .in3(register_1_q[3]),
    .in4(register_1_q[4]), .in5(register_1_q[5]), .in6(1'b0), .in7(1'b1), .out(multiplexer_5_out),
    .sel({Func2[0], Func3}));
  and and_2 (JUMP, multiplexer_5_out, JMPIF);
  and and_3 (FetchReg, ~Func3[0], Func3[1], Func2[0], JMPIF);  // AND_Gate

  // Other names for the same wires on the sheet: Ra[2:0] = ImmV[2:0]; Rd[2:0] = ImmV[5:3]; ImmV[7:6] = Func3;
  //   Sel[3:0] = {Func2, Func3}; Func3[2] = Func2[0]; HL = Func2[0]; JmpAddr[15:0] = Addr

  // Notes on the sheet:
  //   contents of rom_1 (hex, n*v repeats v):
  //   d240 d328 d360 d360 d378 d100 d2b8 d378 d390 d360 d320 0 ffff 8008 6378 d378 6961 d160 2001 6011
  //   8008 6100 d100 6ab9 d2b8 2001 6019 8008 6378 d378 6b91 d390 2001 6021 8008 6360 d360 6b21 d320 2001
  //   6029 8008 6108 d108 6801 d000 2001 6031 8008 0 61ae bc06 0 0 60de b006 0 60de b406 0 60de a006 0
  //   60de a406 0 60de a806 0 60de bc06 0 c002 c803 d7f8 dff8 0 ffff 65450*0 d328 2291 6ffe 67c7 21f7 b407
  //   0 ffff
endmodule

module RegisterBank (
  input  clk,
  input  [15:0] in_val,
  input  Write,
  input  [2:0] Ra,
  input  [2:0] Rd,
  input  [2:0] Rb,
  output [15:0] out_a,
  output [15:0] out_b,
  output [15:0] out_d
);

  wire demultiplexer_1_out0, demultiplexer_1_out1, demultiplexer_1_out2, demultiplexer_1_out3,
       demultiplexer_1_out4, demultiplexer_1_out5, demultiplexer_1_out6, demultiplexer_1_out7;
  wire [15:0] register_1_q, register_2_q, register_3_q, register_4_q, register_5_q, register_6_q,
       register_7_q, register_8_q;

  Demultiplexer #(.select(3)) demultiplexer_1 (
    .out0(demultiplexer_1_out0), .out1(demultiplexer_1_out1), .out2(demultiplexer_1_out2),
    .out3(demultiplexer_1_out3), .out4(demultiplexer_1_out4), .out5(demultiplexer_1_out5),
    .out6(demultiplexer_1_out6), .out7(demultiplexer_1_out7), .in(Write), .sel(Rd));
  Register #(.trigger("falling"), .width(16)) register_1 (
    .D(in_val), .en(demultiplexer_1_out0), .clk(clk), .Q(register_1_q));  // open: clr
  Register #(.trigger("falling"), .width(16)) register_2 (
    .D(in_val), .en(demultiplexer_1_out1), .clk(clk), .Q(register_2_q));  // open: clr
  Register #(.trigger("falling"), .width(16)) register_3 (
    .D(in_val), .en(demultiplexer_1_out2), .clk(clk), .Q(register_3_q));  // open: clr
  Register #(.trigger("falling"), .width(16)) register_4 (
    .D(in_val), .en(demultiplexer_1_out3), .clk(clk), .Q(register_4_q));  // open: clr
  Register #(.trigger("falling"), .width(16)) register_5 (
    .D(in_val), .en(demultiplexer_1_out4), .clk(clk), .Q(register_5_q));  // open: clr
  Register #(.trigger("falling"), .width(16)) register_6 (
    .D(in_val), .en(demultiplexer_1_out5), .clk(clk), .Q(register_6_q));  // open: clr
  Register #(.trigger("falling"), .width(16)) register_7 (
    .D(in_val), .en(demultiplexer_1_out6), .clk(clk), .Q(register_7_q));  // open: clr
  Register #(.trigger("falling"), .width(16)) register_8 (
    .D(in_val), .en(demultiplexer_1_out7), .clk(clk), .Q(register_8_q));  // open: clr
  Multiplexer #(.select(3), .width(16)) multiplexer_1 (
    .in0(register_1_q), .in1(register_2_q), .in2(register_3_q), .in3(register_4_q), .in4(register_5_q),
    .in5(register_6_q), .in6(register_7_q), .in7(register_8_q), .out(out_a), .sel(Ra));
  Multiplexer #(.select(3), .width(16)) multiplexer_2 (
    .in0(register_1_q), .in1(register_2_q), .in2(register_3_q), .in3(register_4_q), .in4(register_5_q),
    .in5(register_6_q), .in6(register_7_q), .in7(register_8_q), .out(out_b), .sel(Rb));
  Multiplexer #(.select(3), .width(16)) multiplexer_3 (
    .in0(register_1_q), .in1(register_2_q), .in2(register_3_q), .in3(register_4_q), .in4(register_5_q),
    .in5(register_6_q), .in6(register_7_q), .in7(register_8_q), .out(out_d), .sel(Rd));
endmodule

module ArithmeticLogicUnit (
  input  [15:0] NumA,
  input  [15:0] NumB,
  input  [3:0] Sel,
  output [15:0] NumOut,
  output [5:0] Status
);

  wire [15:0] adder_1_out, and_1_out, divider_1_out, divider_1_rem, multiplier_1_out, nand_1_out, nor_1_out,
       not_1_out, or_1_out, shifter_1_out, shifter_2_out, shifter_3_out, subtractor_1_out, xnor_1_out,
       xor_1_out;

  Adder #(.width(16)) adder_1 (.a(NumA), .b(NumB), .out(adder_1_out));  // open: cin, cout
  Subtractor #(.width(16)) subtractor_1 (.a(NumA), .b(NumB), .out(subtractor_1_out));  // open: bin, bout
  Multiplier #(.width(16)) multiplier_1 (.a(NumA), .b(NumB), .out(multiplier_1_out));  // open: cin, cout
  Divider #(.width(16)) divider_1 (.a(NumA), .b(NumB), .out(divider_1_out), .rem(divider_1_rem));  // open: upper
  Shifter #(.width(16)) shifter_1 (.in(NumA), .\dist (NumB[3:0]), .out(shifter_1_out));
  Shifter #(.shift("lr"), .width(16)) shifter_2 (.in(NumA), .\dist (NumB[3:0]), .out(shifter_2_out));
  Shifter #(.shift("ar"), .width(16)) shifter_3 (.in(NumA), .\dist (NumB[3:0]), .out(shifter_3_out));
  assign and_1_out = NumA & NumB;  // AND_Gate and_1, 16 bits wide
  assign nand_1_out = ~(NumA & NumB);  // NAND_Gate nand_1, 16 bits wide
  assign or_1_out = NumA | NumB;  // OR_Gate or_1, 16 bits wide
  assign nor_1_out = ~(NumA | NumB);  // NOR_Gate nor_1, 16 bits wide
  assign xor_1_out = NumA ^ NumB;  // XOR_Gate xor_1, 16 bits wide
  assign xnor_1_out = ~(NumA ^ NumB);  // XNOR_Gate xnor_1, 16 bits wide
  assign not_1_out = ~NumB;  // NOT_Gate not_1, 16 bits wide
  Comparator #(.width(16)) comparator_1 (.a(NumA), .b(NumB), .gt(Status[0]), .eq(Status[1]), .lt(Status[2]));
  Comparator #(.mode("unsigned"), .width(16)) comparator_2 (
    .a(NumA), .b(NumB), .gt(Status[3]), .eq(Status[4]), .lt(Status[5]));
  Multiplexer #(.select(4), .width(16)) multiplexer_1 (
    .in0(adder_1_out), .in1(subtractor_1_out), .in2(multiplier_1_out), .in3(divider_1_out),
    .in4(divider_1_rem), .in5(shifter_1_out), .in6(shifter_2_out), .in7(shifter_3_out), .in8(and_1_out),
    .in9(nand_1_out), .in10(or_1_out), .in11(nor_1_out), .in12(xor_1_out), .in13(xnor_1_out),
    .in14(not_1_out), .in15(NumB), .out(NumOut), .sel(Sel));
endmodule

module LogicUnit (
  input  [15:0] A,
  input  [15:0] B,
  input  f2,
  input  f0,
  output [15:0] Y
);

  wire [15:0] and_1_out, or_1_out, xor_1_out;

  assign and_1_out = A & B;  // AND_Gate and_1, 16 bits wide
  assign or_1_out = A | B;  // OR_Gate or_1, 16 bits wide
  assign xor_1_out = A ^ B;  // XOR_Gate xor_1, 16 bits wide
  Multiplexer #(.select(2), .width(16)) multiplexer_1 (
    .in0(and_1_out), .in1(or_1_out), .in2(xor_1_out), .in3(B), .out(Y), .sel({f2, f0}));
endmodule

module ArithmeticUnit (
  input  [15:0] B,
  input  [15:0] A,
  input  Cin,
  output [15:0] Y,
  output overflow,
  output Cout
);

  wire adder_1_cout;

  Adder #(.width(15)) adder_1 (.a(B[14:0]), .b(A[14:0]), .out(Y[14:0]), .cin(Cin), .cout(adder_1_cout));
  Adder #(.width(1)) adder_2 (.a(B[15]), .b(A[15]), .out(Y[15]), .cin(adder_1_cout), .cout(Cout));
  xor xor_1 (overflow, adder_1_cout, Cout);
endmodule

module CPU (
  input  Manual,
  input  [15:0] ManualINST
);

  wire clk, HALT, IO, JMPIF, JUMP, LOAD, LOADI, MATH, multiplexer_3_out, NOOP, or_1_out, or_2_out, STORE;
  wire [0:0] Func3;
  wire [1:0] Func2;
  wire [2:0] controlled_buffer_3_out, Rb;
  wire [5:0] Arithmetic_Logic_Unit_status, register_1_q;
  wire [6:0] ImmV;
  wire [15:0] Addr, Arithmetic_Logic_Unit_numout, controlled_buffer_1_out, DataIN, DataOUT,
       Instruction_Register_q, JmpAddr, multiplexer_1_out, Program_Counter_q, Register_Bank_out_a,
       Register_Bank_out_b, rom_1_data;
  wire [15:13] multiplexer_2_out;

  RAM #(.addrWidth(16), .dataWidth(16)) ram_1 (
    .addr(Addr), .we(STORE), .oe(LOAD), .clk(clk), .din(DataOUT), .dout(DataIN));
  Clock clock_1 (.out(clk));
  ROM #(.addrWidth(16), .dataWidth(16)) rom_1 (.addr(Program_Counter_q), .data(rom_1_data));
  Counter #(.max('hffff), .width(16)) Program_Counter (
    .load(JUMP), .D(JmpAddr), .Q(Program_Counter_q), .clk(clk));  // open: count, carry, up, clr
  assign controlled_buffer_1_out = LOAD ? DataIN : 16'bz;  // Controlled_Buffer controlled_buffer_1
  assign controlled_buffer_1_out = LOADI ? multiplexer_1_out : 16'bz;  // Controlled_Buffer controlled_buffer_2
  Multiplexer #(.width(16)) multiplexer_1 (
    .in0({{8{1'b0}}, Func3[0], ImmV}), .in1({Func3[0], ImmV, {8{1'b0}}}), .out(multiplexer_1_out),
    .sel(Func2[0]));
  assign controlled_buffer_3_out = MATH ? ImmV[5:3] : 3'bz;  // Controlled_Buffer controlled_buffer_3
  assign controlled_buffer_3_out = or_1_out ? Rb : 3'bz;  // Controlled_Buffer controlled_buffer_4
  or or_1 (or_1_out, LOAD, LOADI);
  Register #(.width(16)) Instruction_Register (
    .D(rom_1_data), .en(1'b1), .clk(clk), .Q(Instruction_Register_q));  // open: clr
  assign controlled_buffer_1_out = MATH ? Arithmetic_Logic_Unit_numout : 16'bz;  // Controlled_Buffer controlled_buffer_5
  or or_2 (or_2_out, MATH, LOAD, LOADI);
  Multiplexer #(.width(16)) multiplexer_2 (
    .in0(Instruction_Register_q), .in1(ManualINST), .out({multiplexer_2_out, Func2, Func3[0], ImmV, Rb}),
    .sel(Manual));
  assign Addr = STORE ? Register_Bank_out_a : 16'bz;  // Controlled_Buffer controlled_buffer_6
  RegisterBank Register_Bank (
    .clk(clk), .in_val(controlled_buffer_1_out), .Write(or_2_out), .Ra(ImmV[2:0]),
    .Rd(controlled_buffer_3_out), .Rb(Rb), .out_a(Register_Bank_out_a), .out_b(Register_Bank_out_b));  // open: out_d
  assign Addr = LOAD ? Register_Bank_out_a : 16'bz;  // Controlled_Buffer controlled_buffer_7
  Decoder #(.enable("false"), .select(3)) decoder_1 (
    .out0(NOOP), .out1(MATH), .out2(LOAD), .out3(LOADI), .out4(STORE), .out5(JMPIF), .out6(IO), .out7(HALT),
    .sel(multiplexer_2_out));
  assign DataOUT = STORE ? Register_Bank_out_b : 16'bz;  // Controlled_Buffer controlled_buffer_8
  assign JmpAddr = JMPIF ? Register_Bank_out_b : 16'bz;  // Controlled_Buffer controlled_buffer_9
  Register #(.width(6)) register_1 (
    .D(Arithmetic_Logic_Unit_status), .en(MATH), .clk(clk), .Q(register_1_q));  // open: clr
  ArithmeticLogicUnit Arithmetic_Logic_Unit (
    .NumA(Register_Bank_out_a), .NumB(Register_Bank_out_b), .Sel({Func2, Func3[0], ImmV[6]}),
    .NumOut(Arithmetic_Logic_Unit_numout), .Status(Arithmetic_Logic_Unit_status));
  Pull_Resistor pull_resistor_1 (.node(register_1_q));
  Multiplexer #(.select(3)) multiplexer_3 (
    .in0(register_1_q[0]), .in1(register_1_q[1]), .in2(register_1_q[2]), .in3(register_1_q[3]),
    .in4(register_1_q[4]), .in5(register_1_q[5]), .in6(1'b0), .in7(1'b1), .out(multiplexer_3_out),
    .sel({Func2, Func3[0]}));
  and and_1 (JUMP, multiplexer_3_out, JMPIF);

  // Other names for the same wires on the sheet: Ra[2:0] = ImmV[2:0]; Rd[2:0] = ImmV[5:3];
  //   Sel[3:0] = {Func2, Func3[0], ImmV[6]}; ImmV[7] = Func3[0]; Func3[2:1] = Func2; HL = Func2[0]
endmodule

module KeyboardBuffer (
  input  [6:0] dataIn,
  input  clk,
  input  READY,
  input  READ,
  output KeyboardRead,
  output [15:0] dataOut
);

  wire and_1_out, and_2_out, and_3_out, d_ff_1_q, s_r_ff_1_q, s_r_ff_1_qn, s_r_ff_2_q, s_r_ff_2_qn;
  wire [6:0] register_1_q, register_2_q;

  Pull_Resistor pull_resistor_1 (.node(KeyboardRead));
  assign KeyboardRead = s_r_ff_1_qn ? s_r_ff_1_qn : 1'bz;  // Controlled_Buffer controlled_buffer_1
  assign KeyboardRead = and_2_out ? and_2_out : 1'bz;  // Controlled_Buffer controlled_buffer_2
  S_R_Flip_Flop s_r_ff_1 (
    .S(READY), .R(and_1_out), .clk(clk), .Q(s_r_ff_1_q), .reset(and_1_out), .Qn(s_r_ff_1_qn));  // open: preset
  and and_1 (and_1_out, READ, s_r_ff_2_q);
  Register #(.width(7)) register_1 (.D(dataIn), .en(s_r_ff_1_qn), .clk(clk), .Q(register_1_q));  // open: clr
  Register #(.width(7)) register_2 (.D(dataIn), .en(and_2_out), .clk(clk), .Q(register_2_q));  // open: clr
  and and_2 (and_2_out, s_r_ff_1_q, s_r_ff_2_qn);
  S_R_Flip_Flop s_r_ff_2 (
    .S(s_r_ff_1_q), .R(and_1_out), .clk(clk), .Q(s_r_ff_2_q), .reset(and_1_out), .Qn(s_r_ff_2_qn));  // open: preset
  D_Flip_Flop d_ff_1 (.D(s_r_ff_2_q), .clk(clk), .Q(d_ff_1_q));  // open: Qn, preset, reset
  and and_3 (and_3_out, READ, d_ff_1_q);
  assign dataOut = and_3_out ? {2'b00, register_2_q, register_1_q} : 16'bz;  // Controlled_Buffer controlled_buffer_3
endmodule

module ScreenBuffer (
  input  clk,
  input  [15:0] dataIn,
  input  WRITE,
  output ScreenWrite,
  output [6:0] dataOut
);

  wire decoder_1_out1, decoder_1_out2;
  wire [1:0] counter_1_q;
  wire [15:0] register_1_q;

  Register #(.width(16)) register_1 (.D(dataIn), .en(WRITE), .clk(clk), .Q(register_1_q));  // open: clr
  Counter #(.max('h3), .ongoal("stay"), .width(2)) counter_1 (
    .load(WRITE), .D(2'b00), .Q(counter_1_q), .clk(clk));  // open: count, carry, up, clr
  Multiplexer #(.width(7)) multiplexer_1 (
    .in0(register_1_q[6:0]), .in1(register_1_q[13:7]), .out(dataOut), .sel(decoder_1_out2));
  Decoder #(.enable("false"), .select(2)) decoder_1 (
    .out1(decoder_1_out1), .out2(decoder_1_out2), .sel(counter_1_q));  // open: out0, out3
  or or_1 (ScreenWrite, decoder_1_out1, decoder_1_out2);
endmodule
